# Fritzing sketch blink_led (saved by Fritzing 0.9.0b)
breadboards: 1

parts:
  Raspberry_Pi_1 = Raspberry Pi 3
  R2 = Resistor [tolerance=±5% resistance=150 package="0603 [SMD]"]
  LED1 = LED - 5mm [color="Red (633nm)" package="5 mm [THT]"]

nets:
  N1: Raspberry_Pi_1.3v3, LED1.anode
  N2: Raspberry_Pi_1.GIPO22, R2.Pin_0
  N3: R2.Pin_1, LED1.cathode
