# Fritzing sketch pin_interaction (saved by Fritzing 0.9.0b)
breadboards: 1

parts:
  Raspberry_Pi_1 = Raspberry Pi 3
  R1 = Resistor [tolerance=±5% resistance=150 package="0603 [SMD]"]
  R2 = Resistor [tolerance=±5% resistance=150 package="0603 [SMD]"]
  LED1 = LED - 5mm [color="Red (633nm)" package="5 mm [THT]"]
  Part1 = Max Power IR LED Kit

nets:
  3V3: Raspberry_Pi_1.3v3, R1.Pin_0, Part1.VCC
  N1: Raspberry_Pi_1.GIPO22, R2.Pin_0
  N2: Raspberry_Pi_1.GIPO5, Part1.CONTROL
  GND: Raspberry_Pi_1.GND, Part1.GND
  N3: R1.Pin_1, LED1.anode
  N4: R2.Pin_1, LED1.cathode
