# Fritzing sketch shutdown_button (saved by Fritzing 0.9.0b)
breadboards: 1

parts:
  Raspberry_Pi_1 = Raspberry Pi 3
  Grove1 = Grove Button

nets:
  3V3: Raspberry_Pi_1.3v3, Grove1.VCC
  N1: Raspberry_Pi_1.GIPO18, Grove1.SIG
  GND: Raspberry_Pi_1.GND, Grove1.GND
